// Digital circuit ALU.dig as structural Verilog
module ALU (
  input  [15:0] b,
  input  [15:0] a,
  input  [3:0] s,
  output overflow,
  output zero,
  output [15:0] r
);

  wire alu1_1_co, alu1_2_co, alu1_3_co, alu1_4_co, alu1_5_co, alu1_6_co, alu1_7_co, alu1_8_co, alu1_9_co,
       alu1_10_co, alu1_11_co, alu1_12_co, alu1_13_co, alu1_14_co, alu1_15_co, alumsb_1_p8;

  ALU1 alu1_1 (.a(a[0]), .b(b[0]), .less(alumsb_1_p8), .ci(s[2]), .s(s), .r(r[0]), .co(alu1_1_co));
  ALU1 alu1_2 (.a(a[1]), .b(b[1]), .less(1'b0), .ci(alu1_1_co), .s(s), .r(r[1]), .co(alu1_2_co));
  ALU1 alu1_3 (.a(a[2]), .b(b[2]), .less(1'b0), .ci(alu1_2_co), .s(s), .r(r[2]), .co(alu1_3_co));
  ALU1 alu1_4 (.a(a[3]), .b(b[3]), .less(1'b0), .ci(alu1_3_co), .s(s), .r(r[3]), .co(alu1_4_co));
  ALU1 alu1_5 (.a(a[4]), .b(b[4]), .less(1'b0), .ci(alu1_4_co), .s(s), .r(r[4]), .co(alu1_5_co));
  ALU1 alu1_6 (.a(a[5]), .b(b[5]), .less(1'b0), .ci(alu1_5_co), .s(s), .r(r[5]), .co(alu1_6_co));
  ALU1 alu1_7 (.a(a[6]), .b(b[6]), .less(1'b0), .ci(alu1_6_co), .s(s), .r(r[6]), .co(alu1_7_co));
  ALU1 alu1_8 (.a(a[7]), .b(b[7]), .less(1'b0), .ci(alu1_7_co), .s(s), .r(r[7]), .co(alu1_8_co));
  ALU1 alu1_9 (.a(a[8]), .b(b[8]), .less(1'b0), .ci(alu1_8_co), .s(s), .r(r[8]), .co(alu1_9_co));
  ALU1 alu1_10 (.a(a[9]), .b(b[9]), .less(1'b0), .ci(alu1_9_co), .s(s), .r(r[9]), .co(alu1_10_co));
  ALU1 alu1_11 (.a(a[10]), .b(b[10]), .less(1'b0), .ci(alu1_10_co), .s(s), .r(r[10]), .co(alu1_11_co));
  ALU1 alu1_12 (.a(a[11]), .b(b[11]), .less(1'b0), .ci(alu1_11_co), .s(s), .r(r[11]), .co(alu1_12_co));
  ALU1 alu1_13 (.a(a[12]), .b(b[12]), .less(1'b0), .ci(alu1_12_co), .s(s), .r(r[12]), .co(alu1_13_co));
  ALU1 alu1_14 (.a(a[13]), .b(b[13]), .less(1'b0), .ci(alu1_13_co), .s(s), .r(r[13]), .co(alu1_14_co));
  ALU1 alu1_15 (.a(a[14]), .b(b[14]), .less(1'b0), .ci(alu1_14_co), .s(s), .r(r[14]), .co(alu1_15_co));
  // ALUmsb alumsb_1: pin names not known; wires that end beside it: a[15], b[15], 1'b0, alu1_15_co, s, r[15], overflow, alumsb_1_p8
  nor nor_1 (zero, r[0], r[1], r[2], r[3], r[4], r[5], r[6], r[7], r[8], r[9], r[10], r[11], r[12], r[13], r[14], r[15]);
endmodule
