// Digital circuit ALU1.dig as structural Verilog
module ALU1 (
  input  a,
  input  b,
  input  less,
  input  ci,
  input  [3:0] s,
  output r,
  output co
);

  wire add_1_s, and_1_out, multiplexer_1_out, multiplexer_2_out, not_1_out, not_2_out, or_1_out;

  not not_1 (not_1_out, a);
  not not_2 (not_2_out, b);
  Multiplexer multiplexer_1 (.sel(s[3]), .in_0(a), .in_1(not_1_out), .out(multiplexer_1_out));
  Multiplexer multiplexer_2 (.sel(s[2]), .in_0(b), .in_1(not_2_out), .out(multiplexer_2_out));
  and and_1 (and_1_out, multiplexer_1_out, multiplexer_2_out);
  or or_1 (or_1_out, multiplexer_1_out, multiplexer_2_out);
  Add add_1 (.a(multiplexer_1_out), .b(multiplexer_2_out), .c_i(ci), .s(add_1_s), .c_o(co));
  Multiplexer #(.Selector_Bits(2)) multiplexer_3 (
    .sel(s[1:0]), .in_0(and_1_out), .in_1(or_1_out), .in_2(add_1_s), .in_3(less), .out(r));

  // Notes on the sheet:
  //   na
  //   nb
  //   A
  //   B
  //   r0
  //   r1
  //   r2
endmodule
