// Digital circuit ALUmsb.dig as structural Verilog
module ALUmsb (
  input  a,
  input  b,
  input  less,
  input  ci,
  input  [3:0] s,
  output r,
  output of,
  output set
);

  wire add_1_c_o, and_1_out, multiplexer_1_out, multiplexer_2_out, not_1_out, not_2_out, or_1_out, xor_1_out;

  not not_1 (not_1_out, a);
  not not_2 (not_2_out, b);
  Multiplexer multiplexer_1 (.sel(s[3]), .in_0(a), .in_1(not_1_out), .out(multiplexer_1_out));
  Multiplexer multiplexer_2 (.sel(s[2]), .in_0(b), .in_1(not_2_out), .out(multiplexer_2_out));
  and and_1 (and_1_out, multiplexer_1_out, multiplexer_2_out);
  or or_1 (or_1_out, multiplexer_1_out, multiplexer_2_out);
  Add add_1 (.a(multiplexer_1_out), .b(multiplexer_2_out), .c_i(ci), .s(set), .c_o(add_1_c_o));
  xor xor_1 (xor_1_out, add_1_c_o, ci);
  Multiplexer #(.Selector_Bits(2)) multiplexer_3 (
    .sel(s[1:0]), .in_0(and_1_out), .in_1(or_1_out), .in_2(set), .in_3(less), .out(r));
  and and_2 (of, s[1], xor_1_out);
  // Pins of 3 and 4 bits meet at s

  // Notes on the sheet:
  //   na
  //   nb
  //   A
  //   B
  //   r0
  //   r1
  //   co
  //   of0
endmodule
