// Digital circuit BranchControl.dig as structural Verilog
module BranchControl (
  input  BEQ,
  input  BNE,
  input  Zero,
  output Taken
);

  wire and_1_out, and_2_out, not_1_out;

  not not_1 (not_1_out, Zero);
  and and_1 (and_1_out, BEQ, Zero);
  and and_2 (and_2_out, BNE, not_1_out);
  or or_1 (Taken, and_1_out, and_2_out);

  // Notes on the sheet:
  //   NotZero
  //   BeqTaken
  //   BneTaken
endmodule
