// Digital circuit CPU.dig as structural Verilog
module CPU (
  input  clock
);

  wire IDEX_ALUSrc_q, IDEX_RegDst_q, reg_fwd_sel_1_fwd, reg_fwd_sel_2_fwd, rf_p5;
  wire [1:0] IDEX_rd_q, IDEX_rt_q, IFID_IR_q_2, IFID_IR_q_3, IFID_IR_q_4, rf_p3;
  wire [3:0] IDEX_ALUctl_q, IFID_IR_q_5, MainControl_d;
  wire [5:0] IFID_IR_q;
  wire [6:4] MainControl_d_2;
  wire [15:0] bitextender_1_out, fetch_r, IDEX_RD1_q, IDEX_RD2_q, IDEX_SignExt_q, IMemory_d,
       multiplexer_1_out, multiplexer_2_out, multiplexer_4_out, PC_q, rf_p4, rf_p7, rf_p8;

  Register #(.Bits(16), .isProgramCounter("true")) PC (.D(fetch_r), .C(clock), .en(1'b1), .Q(PC_q));
  ALU fetch (.r(fetch_r), .a(PC_q), .b(16'h2), .s(4'b0010));  // open: zero, overflow
  ROM #(.AddrBits(16), .Bits(16)) IMemory (.A(PC_q), .sel(1'b1), .D(IMemory_d));
  Register #(.Bits(16)) IFID_IR (
    .D(IMemory_d), .C(clock), .en(1'b1), .Q({IFID_IR_q_5, IFID_IR_q_4, IFID_IR_q_3, IFID_IR_q_2, IFID_IR_q}));
  ROM #(.AddrBits(4), .Bits(7)) MainControl (.A(IFID_IR_q_5), .sel(1'b1), .D({MainControl_d_2, MainControl_d}));
  // reg_file rf: pin names not known; wires that end beside it: IFID_IR_q_4, IFID_IR_q_3, rf_p3, rf_p4, rf_p5, clock, rf_p7, rf_p8
  reg_fwd_sel reg_fwd_sel_1 (.WR(IFID_IR_q_4), .IR(rf_p3), .WE(rf_p5), .FWD(reg_fwd_sel_1_fwd));
  reg_fwd_sel reg_fwd_sel_2 (.WR(IFID_IR_q_3), .IR(rf_p3), .WE(rf_p5), .FWD(reg_fwd_sel_2_fwd));
  BitExtender bitextender_1 (.in({IFID_IR_q_2, IFID_IR_q}), .out(bitextender_1_out));
  Multiplexer #(.Bits(16)) multiplexer_1 (.sel(reg_fwd_sel_1_fwd), .in_0(rf_p7), .in_1(rf_p4), .out(multiplexer_1_out));
  Multiplexer #(.Bits(16)) multiplexer_2 (.sel(reg_fwd_sel_2_fwd), .in_0(rf_p8), .in_1(rf_p4), .out(multiplexer_2_out));
  Register IDEX_RegWrite (.D(MainControl_d_2[6]), .C(clock), .en(1'b1), .Q(rf_p5));
  Register IDEX_RegDst (.D(MainControl_d_2[5]), .C(clock), .en(1'b1), .Q(IDEX_RegDst_q));
  Register IDEX_ALUSrc (.D(MainControl_d_2[4]), .C(clock), .en(1'b1), .Q(IDEX_ALUSrc_q));
  Register #(.Bits(4)) IDEX_ALUctl (.D(MainControl_d), .C(clock), .en(1'b1), .Q(IDEX_ALUctl_q));
  Register #(.Bits(16)) IDEX_RD1 (.D(multiplexer_1_out), .C(clock), .en(1'b1), .Q(IDEX_RD1_q));
  Register #(.Bits(16)) IDEX_RD2 (.D(multiplexer_2_out), .C(clock), .en(1'b1), .Q(IDEX_RD2_q));
  Register #(.Bits(2)) IDEX_rt (.D(IFID_IR_q_3), .C(clock), .en(1'b1), .Q(IDEX_rt_q));
  Register #(.Bits(2)) IDEX_rd (.D(IFID_IR_q_2), .C(clock), .en(1'b1), .Q(IDEX_rd_q));
  Register #(.Bits(16)) IDEX_SignExt (.D(bitextender_1_out), .C(clock), .en(1'b1), .Q(IDEX_SignExt_q));
  Multiplexer #(.Bits(2)) multiplexer_3 (.sel(IDEX_RegDst_q), .in_0(IDEX_rt_q), .in_1(IDEX_rd_q), .out(rf_p3));
  Multiplexer #(.Bits(16)) multiplexer_4 (
    .sel(IDEX_ALUSrc_q), .in_0(IDEX_RD2_q), .in_1(IDEX_SignExt_q), .out(multiplexer_4_out));
  ALU execution_unit (.r(rf_p4), .a(IDEX_RD1_q), .b(multiplexer_4_out), .s(IDEX_ALUctl_q));  // open: zero, overflow

  // Notes on the sheet:
  //   PCplus2
  //   contents of IMemory (hex, n*v repeats v):
  //   7407,0,7803,0,9100,0,9202,0,8100,0,8202,0,66c0,0,ac02,0,9102,0
  //   ,9200,0,8100,0,8202,0,4a80,0,7a01,0,6c0
  //   IR
  //   IF/ID
  //   contents of MainControl (hex, n*v repeats v):
  //   482,486,480,481,48c,48d,487,282,382,242,26,16
  //   RegWrite
  //   RegDst
  //   ALUSrc
  //   ALUctl
  //   RD1
  //   RD2
  //   WD
  //   TODO bit order
  //   FWD SEL1
  //   FWD SEL2
  //   SignExtend
  //   FWD RD1
  //   FWD RD2
  //   ID/EX
  //   muxReg
  //   B
  //   muxData
  //   WR
  //   ALUOut/WD
endmodule
