// Digital circuit MainControl.dig as structural Verilog
module MainControl (
  input  [3:0] op,
  output RegDistr,
  output Branch,
  output MemRead,
  output MemToReg,
  output [3:0] ALUOp,
  output MemWrite,
  output ALUSrc,
  output RegWrite,
  output BNE
);

  wire and_3_out, and_6_out, and_7_out, and_8_out, and_9_out, and_10_out, and_11_out, and_12_out, and_14_out,
       and_15_out, and_16_out, and_17_out, not_1_out, not_2_out, not_3_out, not_4_out;

  not not_1 (not_1_out, op[0]);
  not not_2 (not_2_out, op[1]);
  not not_3 (not_3_out, op[2]);
  not not_4 (not_4_out, op[3]);
  and and_1 (Branch, op[1], op[3]);
  and and_2 (BNE, not_1_out, op[1], op[3]);
  and and_3 (and_3_out, not_2_out, op[3]);
  and and_4 (MemWrite, op[0], not_2_out, op[3]);
  and and_5 (MemRead, not_1_out, not_2_out, op[3]);
  and and_6 (and_6_out, op[0], op[1], op[2], not_4_out);
  and and_7 (and_7_out, not_3_out, not_4_out);
  and and_8 (and_8_out, not_2_out, not_4_out);
  and and_9 (and_9_out, op[0], not_2_out, not_4_out);
  and and_10 (and_10_out, not_1_out, not_4_out);
  and and_11 (and_11_out, op[1], op[2]);
  and and_12 (and_12_out, not_1_out, op[1], op[2]);
  and and_13 (ALUOp[3], not_2_out, op[2]);
  and and_14 (and_14_out, not_1_out, op[2]);
  and and_15 (and_15_out, op[0], op[1], not_3_out);
  and and_16 (and_16_out, not_2_out, not_3_out);
  and and_17 (and_17_out, not_1_out, not_2_out, not_3_out);
  or or_1 (ALUOp[0], and_15_out, and_12_out, and_9_out, BNE);
  or or_2 (ALUOp[1], and_16_out, and_11_out, op[3]);
  or or_3 (ALUOp[2], and_14_out, ALUOp[3]);
  or or_4 (RegDistr, and_10_out, and_8_out, and_7_out);
  or or_5 (ALUSrc, and_6_out, and_3_out);
  or or_6 (RegWrite, and_17_out, not_4_out);

  assign MemToReg = MemRead;

  // Notes on the sheet:
  //   wy
  //   wyz'
  //   wy'
  //   wy'z
  //   wy'z'
  //   w'xyz
  //   w'x'
  //   w'y'
  //   w'y'z
  //   w'z'
  //   xy
  //   xyz'
  //   xy'
  //   xz'
  //   x'yz
  //   x'y'
  //   x'y'z'
endmodule
