// Digital circuit reg_fwd_sel.dig as structural Verilog
module reg_fwd_sel (
  input  [1:0] WR,
  input  [1:0] IR,
  input  WE,
  output FWD
);

  wire nor_1_out, xor_1_out, xor_2_out;

  xor xor_1 (xor_1_out, IR[0], WR[0]);
  xor xor_2 (xor_2_out, IR[1], WR[1]);
  nor nor_1 (nor_1_out, xor_1_out, xor_2_out);
  and and_1 (FWD, nor_1_out, WE);

  // Notes on the sheet:
  //   ne[0]
  //   ne[1]
  //   eq
endmodule
