// Digital circuit shift_left_1.dig as structural Verilog
module shift_left_1 (
  input  [15:0] in,
  output [15:0] out
);

  // Pins of 1 and 16 bits meet at {in[14:0], 1'b0}

  assign out = {in[14:0], 1'b0};
endmodule
